# Fritzing sketch sketch1 (saved by Fritzing 0.9.3b)
breadboards: 1

parts:
  Součástka1 = Arduino Nano (Rev3.0)  # not connected
  VCC1 = Battery  # not connected
  GLCD_128x1 = 128 x 64 Graphic LCD  # not connected
  S1 = Pushbutton [package="[THT]"]
  S2 = Pushbutton [package="[THT]"]

nets:
  N1: S1.Pin_1, S1.Pin_2
  N2: S1.Pin_3, S1.Pin_4
  N3: S2.Pin_1, S2.Pin_2
  N4: S2.Pin_3, S2.Pin_4
